// Logisim project LateefAfolabi_IFT211_SmartWaterTankMonitoring_ControlSystem_1.circ as structural Verilog: 1 circuit, main circuit main
// CLOCK
module main (
  input  EMPTY,
  input  LEVEL25,
  input  RESET,
  input  LEVEL50,
  input  FULL,
  output STOREDL1,
  output L1,
  output STOREDL0,
  output L0
);

  wire and_2_out, CLOCK, FULL_t, not_1_out, not_2_out, SL0, SL1;
  wire [1:0] counter_1_q;
  wire [3:0] bit_extender_1_out;

  or or_1 (L1, LEVEL50, FULL);
  or or_2 (L0, LEVEL25, FULL);
  and and_1 (FULL_t, L1, L0);
  not not_1 (not_1_out, FULL_t);
  LED PUMP (.in(not_1_out));
  D_Flip_Flop d_ff_1 (.D(L1), .clk(CLOCK), .Q(SL1), .reset(RESET));  // open: Qn, preset
  Clock clock_1 (.out(CLOCK));
  D_Flip_Flop d_ff_2 (.D(L0), .clk(CLOCK), .Q(SL0), .reset(RESET));  // open: Qn, preset
  Bit_Extender #(.in_width(4), .out_width(4)) bit_extender_1 (.in({2'b00, SL1, SL0}), .out(bit_extender_1_out));
  not not_2 (not_2_out, FULL_t);
  Hex_Digit_Display hex_digit_display_1 (.value(bit_extender_1_out));  // open: dp
  Counter #(.max('h3), .width(2)) counter_1 (
    .clr(not_2_out), .load(1'b0), .up(1'b0), .count(FULL_t), .clk(CLOCK), .Q(counter_1_q));  // open: D, carry
  buf and_2 (and_2_out, counter_1_q[0]);  // AND_Gate
  LED L100 (.in(and_2_out));

  // Other names for the same wires on the sheet: FFClock = CLOCK; FFReset = RESET
endmodule
